// Logisim project SD.circ as structural Verilog: 1 circuit, main circuit Mux2
module Mux2 (
  input  A,
  input  B,
  input  Sel,
  output out_4
);

  wire and_1_out, and_2_out;

  and and_1 (and_1_out, A, ~Sel);  // AND_Gate
  and and_2 (and_2_out, B, Sel);
  or or_1 (out_4, and_1_out, and_2_out);
endmodule
